# Fritzing sketch contorfzz (saved by Fritzing 0.9.3b)
breadboards: 1

parts:
  Part1 = Arduino Nano (Rev3.0) (ICSP)
  S1 = Pushbutton [package="[SMD]"]
  R1 = Resistor [tolerance=±5% resistance=220 package="0603 [SMD]"]

nets:
  N1: Part1.GND, R1.Pin_0
  N2: Part1.D5, S1.Pin_3, S1.Pin_4, R1.Pin_1
  N3: Part1.5V, S1.Pin_1, S1.Pin_2
